// Logisim project a4.circ as structural Verilog: 1 circuit, main circuit main
module main (
  input  A,
  input  B,
  input  C,
  input  D,
  input  E,
  input  F,
  output X,
  output Y
);

  wire and_2_out, and_3_out, clock_1_out, clock_2_out, not_1_out;

  // NoConnect on B
  not not_1 (not_1_out, E);
  Clock clock_1 (.out(clock_1_out));
  Clock clock_2 (.out(clock_2_out));
  and and_1 (X, A, clock_2_out, C);
  and and_2 (and_2_out, D, not_1_out, clock_1_out, F);
  and and_3 (and_3_out, D, E, clock_1_out, F);
  or or_1 (Y, and_2_out, and_3_out);

  // Notes on the sheet:
  //   Luyue Guan
  //   2-bit solution
  //   3-bit solution
  //   Student ID: 260950108
endmodule
