// Logisim project a5.circ as structural Verilog: 1 circuit, main circuit main
module main (
  input  in_1,
  input  in_2,
  input  in_3,
  input  in_4,
  input  in_5,
  input  in_6,
  input  in_7,
  input  in_8,
  output out_9,
  output out_10,
  output out_11,
  output out_12
);

  wire and_1_out, and_2_out, and_3_out, and_4_out, and_5_out, and_6_out, and_7_out, and_8_out, and_17_out,
       and_18_out, and_19_out, and_20_out, and_21_out, and_22_out, and_23_out, and_24_out, and_25_out,
       and_26_out, and_27_out, and_28_out, and_29_out, and_30_out, and_31_out, and_32_out, and_33_out,
       and_35_out, and_36_out, and_37_out, and_38_out, and_39_out, and_40_out, and_41_out, and_42_out,
       and_43_out, and_44_out, and_45_out, and_46_out, and_47_out, and_48_out, and_49_out, and_50_out,
       and_51_out, and_52_out, and_53_out, and_54_out, and_55_out, and_56_out, and_57_out, and_58_out,
       and_59_out, and_60_out, and_61_out, and_62_out, and_63_out, and_64_out, and_65_out, and_66_out,
       and_67_out, and_68_out, and_69_out, and_70_out, and_71_out, and_72_out, and_73_out, and_74_out,
       and_75_out, and_76_out, and_77_out, and_78_out, and_79_out, and_80_out, CLK, not_2_out, not_3_out,
       not_4_out, not_5_out, not_6_out, not_7_out, not_8_out, not_9_out, not_10_out, not_11_out, not_12_out,
       not_13_out, not_14_out, not_15_out, not_16_out, not_17_out, not_18_out, not_19_out, not_20_out,
       not_21_out, not_22_out, not_23_out, not_24_out, not_25_out, not_26_out, not_27_out, not_28_out,
       not_29_out, not_30_out, not_31_out, not_32_out, not_33_out, not_34_out, not_35_out, not_36_out,
       not_37_out, not_38_out, not_39_out, not_40_out, not_41_out, not_42_out, not_43_out, not_44_out,
       not_45_out, not_46_out, not_47_out, not_48_out, not_49_out, or_1_out, or_2_out, or_3_out, or_4_out,
       Read, s_r_ff_1_q, s_r_ff_2_q, s_r_ff_3_q, s_r_ff_4_q, s_r_ff_5_q, s_r_ff_6_q, s_r_ff_7_q, s_r_ff_8_q,
       s_r_ff_9_q, s_r_ff_10_q, s_r_ff_11_q, s_r_ff_12_q, s_r_ff_13_q, s_r_ff_14_q, s_r_ff_15_q, s_r_ff_16_q,
       s_r_ff_17_q, s_r_ff_18_q, s_r_ff_19_q, s_r_ff_20_q, s_r_ff_21_q, s_r_ff_22_q, s_r_ff_23_q,
       s_r_ff_24_q, s_r_ff_25_q, s_r_ff_26_q, s_r_ff_27_q, s_r_ff_28_q, s_r_ff_29_q, s_r_ff_30_q,
       s_r_ff_31_q, s_r_ff_32_q, W0, W1, W2, W3, W4, W5, W6, W7;

  not not_1 (Read, in_1);
  // NoConnect on in_2
  // NoConnect on in_3
  // NoConnect on in_4
  not not_2 (not_2_out, in_2);
  not not_3 (not_3_out, in_3);
  not not_4 (not_4_out, in_4);
  not not_5 (not_5_out, in_2);
  not not_6 (not_6_out, in_3);
  not not_7 (not_7_out, in_2);
  not not_8 (not_8_out, in_4);
  not not_9 (not_9_out, in_2);
  not not_10 (not_10_out, in_3);
  not not_11 (not_11_out, in_4);
  not not_12 (not_12_out, in_3);
  not not_13 (not_13_out, in_4);
  and and_1 (and_1_out, not_2_out, not_3_out, not_4_out);
  and and_2 (and_2_out, not_5_out, not_6_out, in_4);
  and and_3 (and_3_out, not_7_out, in_3, not_8_out);
  and and_4 (and_4_out, not_9_out, in_3, in_4);
  and and_5 (and_5_out, in_2, not_10_out, not_11_out);
  and and_6 (and_6_out, in_2, not_12_out, in_4);
  and and_7 (and_7_out, in_2, in_3, not_13_out);
  and and_8 (and_8_out, in_2, in_3, in_4);
  and and_9 (W0, and_1_out, in_1);
  and and_10 (W1, and_2_out, in_1);
  and and_11 (W2, and_3_out, in_1);
  and and_12 (W3, and_4_out, in_1);
  and and_13 (W4, and_5_out, in_1);
  and and_14 (W5, and_6_out, in_1);
  and and_15 (W6, and_7_out, in_1);
  and and_16 (W7, and_8_out, in_1);
  // NoConnect on in_5
  // NoConnect on in_6
  // NoConnect on in_7
  // NoConnect on in_8
  and and_17 (and_17_out, in_5, W0);
  and and_18 (and_18_out, in_6, W0);
  and and_19 (and_19_out, in_7, W0);
  and and_20 (and_20_out, in_8, W0);
  and and_21 (and_21_out, in_5, W1);
  and and_22 (and_22_out, in_6, W1);
  and and_23 (and_23_out, in_7, W1);
  and and_24 (and_24_out, in_8, W1);
  and and_25 (and_25_out, in_5, W2);
  and and_26 (and_26_out, in_6, W2);
  and and_27 (and_27_out, in_7, W2);
  and and_28 (and_28_out, in_8, W2);
  and and_29 (and_29_out, in_5, W3);
  and and_30 (and_30_out, in_6, W3);
  and and_31 (and_31_out, in_7, W3);
  and and_32 (and_32_out, in_8, W3);
  and and_33 (and_33_out, in_5, W4);
  and and_34 (W4, in_6, W4);
  and and_35 (and_35_out, in_7, W4);
  and and_36 (and_36_out, in_8, W4);
  and and_37 (and_37_out, in_5, W5);
  and and_38 (and_38_out, in_6, W5);
  and and_39 (and_39_out, in_7, W5);
  and and_40 (and_40_out, in_8, W5);
  and and_41 (and_41_out, in_5, W6);
  and and_42 (and_42_out, in_6, W6);
  and and_43 (and_43_out, in_7, W6);
  and and_44 (and_44_out, in_8, W6);
  and and_45 (and_45_out, in_5, W7);
  and and_46 (and_46_out, in_6, W7);
  and and_47 (and_47_out, in_7, W7);
  and and_48 (and_48_out, in_8, W7);
  not not_14 (not_14_out, and_17_out);
  not not_15 (not_15_out, and_18_out);
  not not_16 (not_16_out, and_19_out);
  not not_17 (not_17_out, and_20_out);
  not not_18 (not_18_out, and_21_out);
  not not_19 (not_19_out, and_22_out);
  not not_20 (not_20_out, and_23_out);
  not not_21 (not_21_out, and_24_out);
  not not_22 (not_22_out, and_25_out);
  not not_23 (not_23_out, and_26_out);
  not not_24 (not_24_out, and_27_out);
  not not_25 (not_25_out, and_28_out);
  not not_26 (not_26_out, and_29_out);
  not not_27 (not_27_out, and_30_out);
  not not_28 (not_28_out, and_31_out);
  not not_29 (not_29_out, and_32_out);
  not not_30 (not_30_out, and_33_out);
  not not_31 (not_31_out, W4);
  not not_32 (not_32_out, and_35_out);
  not not_33 (not_33_out, and_36_out);
  not not_34 (not_34_out, and_37_out);
  not not_35 (not_35_out, and_38_out);
  not not_36 (not_36_out, and_39_out);
  not not_37 (not_37_out, and_40_out);
  not not_38 (not_38_out, and_41_out);
  not not_39 (not_39_out, and_42_out);
  not not_40 (not_40_out, and_43_out);
  not not_41 (not_41_out, and_44_out);
  not not_42 (not_42_out, and_45_out);
  not not_43 (not_43_out, and_46_out);
  not not_44 (not_44_out, and_47_out);
  not not_45 (not_45_out, and_48_out);
  and and_49 (and_49_out, not_14_out, W0);
  and and_50 (and_50_out, not_15_out, W0);
  and and_51 (and_51_out, not_16_out, W0);
  and and_52 (and_52_out, not_17_out, W0);
  and and_53 (and_53_out, not_18_out, W1);
  and and_54 (and_54_out, not_19_out, W1);
  and and_55 (and_55_out, not_20_out, W1);
  and and_56 (and_56_out, not_21_out, W1);
  S_R_Flip_Flop s_r_ff_1 (.S(and_25_out), .R(and_57_out), .clk(CLK), .Q(s_r_ff_1_q));  // open: reset, Qn, preset
  and and_57 (and_57_out, not_22_out, W2);
  S_R_Flip_Flop s_r_ff_2 (.S(and_26_out), .R(and_58_out), .clk(CLK), .Q(s_r_ff_2_q));  // open: reset, Qn, preset
  and and_58 (and_58_out, not_23_out, W2);
  S_R_Flip_Flop s_r_ff_3 (.S(and_27_out), .R(and_59_out), .clk(CLK), .Q(s_r_ff_3_q));  // open: reset, Qn, preset
  and and_59 (and_59_out, not_24_out, W2);
  S_R_Flip_Flop s_r_ff_4 (.S(and_28_out), .R(and_60_out), .clk(CLK), .Q(s_r_ff_4_q));  // open: reset, Qn, preset
  and and_60 (and_60_out, not_25_out, W2);
  S_R_Flip_Flop s_r_ff_5 (.S(and_29_out), .R(and_61_out), .clk(CLK), .Q(s_r_ff_5_q));  // open: reset, Qn, preset
  and and_61 (and_61_out, not_26_out, W3);
  S_R_Flip_Flop s_r_ff_6 (.S(and_30_out), .R(and_62_out), .clk(CLK), .Q(s_r_ff_6_q));  // open: reset, Qn, preset
  and and_62 (and_62_out, not_27_out, W3);
  S_R_Flip_Flop s_r_ff_7 (.S(and_31_out), .R(and_63_out), .clk(CLK), .Q(s_r_ff_7_q));  // open: reset, Qn, preset
  and and_63 (and_63_out, not_28_out, W3);
  S_R_Flip_Flop s_r_ff_8 (.S(and_32_out), .R(and_64_out), .clk(CLK), .Q(s_r_ff_8_q));  // open: reset, Qn, preset
  and and_64 (and_64_out, not_29_out, W3);
  S_R_Flip_Flop s_r_ff_9 (.S(and_33_out), .R(and_65_out), .clk(CLK), .Q(s_r_ff_9_q));  // open: reset, Qn, preset
  and and_65 (and_65_out, not_30_out, W4);
  S_R_Flip_Flop s_r_ff_10 (.S(W4), .R(and_66_out), .clk(CLK), .Q(s_r_ff_10_q));  // open: reset, Qn, preset
  and and_66 (and_66_out, not_31_out, W4);
  S_R_Flip_Flop s_r_ff_11 (.S(and_35_out), .R(and_67_out), .clk(CLK), .Q(s_r_ff_11_q));  // open: reset, Qn, preset
  and and_67 (and_67_out, not_32_out, W4);
  S_R_Flip_Flop s_r_ff_12 (.S(and_36_out), .R(and_68_out), .clk(CLK), .Q(s_r_ff_12_q));  // open: reset, Qn, preset
  and and_68 (and_68_out, not_33_out, W4);
  S_R_Flip_Flop s_r_ff_13 (.S(and_37_out), .R(and_69_out), .clk(CLK), .Q(s_r_ff_13_q));  // open: reset, Qn, preset
  and and_69 (and_69_out, not_34_out, W5);
  S_R_Flip_Flop s_r_ff_14 (.S(and_38_out), .R(and_70_out), .clk(CLK), .Q(s_r_ff_14_q));  // open: reset, Qn, preset
  and and_70 (and_70_out, not_35_out, W5);
  S_R_Flip_Flop s_r_ff_15 (.S(and_39_out), .R(and_71_out), .clk(CLK), .Q(s_r_ff_15_q));  // open: reset, Qn, preset
  and and_71 (and_71_out, not_36_out, W5);
  S_R_Flip_Flop s_r_ff_16 (.S(and_40_out), .R(and_72_out), .clk(CLK), .Q(s_r_ff_16_q));  // open: reset, Qn, preset
  and and_72 (and_72_out, not_37_out, W5);
  S_R_Flip_Flop s_r_ff_17 (.S(and_41_out), .R(and_73_out), .clk(CLK), .Q(s_r_ff_17_q));  // open: reset, Qn, preset
  and and_73 (and_73_out, not_38_out, W6);
  S_R_Flip_Flop s_r_ff_18 (.S(and_42_out), .R(and_74_out), .clk(CLK), .Q(s_r_ff_18_q));  // open: reset, Qn, preset
  and and_74 (and_74_out, not_39_out, W6);
  S_R_Flip_Flop s_r_ff_19 (.S(and_43_out), .R(and_75_out), .clk(CLK), .Q(s_r_ff_19_q));  // open: reset, Qn, preset
  and and_75 (and_75_out, not_40_out, W6);
  S_R_Flip_Flop s_r_ff_20 (.S(and_44_out), .R(and_76_out), .clk(CLK), .Q(s_r_ff_20_q));  // open: reset, Qn, preset
  and and_76 (and_76_out, not_41_out, W6);
  S_R_Flip_Flop s_r_ff_21 (.S(and_45_out), .R(and_77_out), .clk(CLK), .Q(s_r_ff_21_q));  // open: reset, Qn, preset
  and and_77 (and_77_out, not_42_out, W7);
  S_R_Flip_Flop s_r_ff_22 (.S(and_46_out), .R(and_78_out), .clk(CLK), .Q(s_r_ff_22_q));  // open: reset, Qn, preset
  and and_78 (and_78_out, not_43_out, W7);
  S_R_Flip_Flop s_r_ff_23 (.S(and_47_out), .R(and_79_out), .clk(CLK), .Q(s_r_ff_23_q));  // open: reset, Qn, preset
  and and_79 (and_79_out, not_44_out, W7);
  S_R_Flip_Flop s_r_ff_24 (.S(and_48_out), .R(and_80_out), .clk(CLK), .Q(s_r_ff_24_q));  // open: reset, Qn, preset
  and and_80 (and_80_out, not_45_out, W7);
  Clock clock_1 (.out(CLK));
  S_R_Flip_Flop s_r_ff_25 (.S(and_17_out), .R(and_49_out), .clk(CLK), .Q(s_r_ff_25_q));  // open: reset, Qn, preset
  S_R_Flip_Flop s_r_ff_26 (.S(and_18_out), .R(and_50_out), .clk(CLK), .Q(s_r_ff_26_q));  // open: reset, Qn, preset
  S_R_Flip_Flop s_r_ff_27 (.S(and_19_out), .R(and_51_out), .clk(CLK), .Q(s_r_ff_27_q));  // open: reset, Qn, preset
  S_R_Flip_Flop s_r_ff_28 (.S(and_20_out), .R(and_52_out), .clk(CLK), .Q(s_r_ff_28_q));  // open: reset, Qn, preset
  S_R_Flip_Flop s_r_ff_29 (.S(and_21_out), .R(and_53_out), .clk(CLK), .Q(s_r_ff_29_q));  // open: reset, Qn, preset
  S_R_Flip_Flop s_r_ff_30 (.S(and_22_out), .R(and_54_out), .clk(CLK), .Q(s_r_ff_30_q));  // open: reset, Qn, preset
  S_R_Flip_Flop s_r_ff_31 (.S(and_23_out), .R(and_55_out), .clk(CLK), .Q(s_r_ff_31_q));  // open: reset, Qn, preset
  S_R_Flip_Flop s_r_ff_32 (.S(and_24_out), .R(and_56_out), .clk(CLK), .Q(s_r_ff_32_q));  // open: reset, Qn, preset
  and and_81 (out_9, or_1_out, not_46_out, Read);
  not not_46 (not_46_out, CLK);
  or or_1 (or_1_out, s_r_ff_25_q, s_r_ff_29_q, s_r_ff_1_q, s_r_ff_5_q, s_r_ff_9_q, s_r_ff_13_q, s_r_ff_17_q, s_r_ff_21_q);
  and and_82 (out_10, or_2_out, not_47_out, Read);
  not not_47 (not_47_out, CLK);
  or or_2 (or_2_out, s_r_ff_26_q, s_r_ff_30_q, s_r_ff_2_q, s_r_ff_6_q, s_r_ff_10_q, s_r_ff_14_q, s_r_ff_18_q, s_r_ff_22_q);
  and and_83 (out_11, or_3_out, not_48_out, Read);
  not not_48 (not_48_out, CLK);
  or or_3 (or_3_out, s_r_ff_27_q, s_r_ff_31_q, s_r_ff_3_q, s_r_ff_7_q, s_r_ff_11_q, s_r_ff_15_q, s_r_ff_19_q, s_r_ff_23_q);
  and and_84 (out_12, or_4_out, not_49_out, Read);
  not not_49 (not_49_out, CLK);
  or or_4 (or_4_out, s_r_ff_28_q, s_r_ff_32_q, s_r_ff_4_q, s_r_ff_8_q, s_r_ff_12_q, s_r_ff_16_q, s_r_ff_20_q, s_r_ff_24_q);

  // Other names for the same wires on the sheet: Mode = in_1
endmodule
