// Logisim project a6.circ as structural Verilog: 1 circuit, main circuit main
module main (
  input  in_1,
  input  in_2,
  input  in_3,
  input  in_4,
  input  in_5,
  input  in_6,
  input  in_7,
  input  in_8,
  input  Add_Sub_command,
  output out_10,
  output out_11,
  output out_12,
  output out_13,
  output out_14,
  output out_15,
  output out_16
);

  wire A, and_1_out, and_3_out, and_4_out, and_6_out, and_8_out, and_9_out, and_11_out, and_12_out,
       and_14_out, and_15_out, and_17_out, and_18_out, and_19_out, and_20_out, and_23_out, and_24_out,
       and_25_out, and_26_out, and_27_out, B, C, clock_1_out, D, not_1_out, not_2_out, not_3_out, not_4_out,
       not_5_out, not_6_out, not_7_out, not_8_out, not_9_out, not_10_out, not_11_out, not_12_out, not_13_out,
       not_14_out, not_15_out, or_1_out, or_2_out, or_4_out, or_5_out, or_6_out, or_7_out, or_8_out, SignO,
       SignR, xor_2_out, xor_3_out, xor_4_out, xor_5_out, xor_6_out, xor_7_out, xor_8_out, xor_9_out,
       xor_10_out, xor_11_out, xor_12_out, xor_13_out;

  Clock clock_1 (.out(clock_1_out));
  and and_1 (and_1_out, or_2_out, xor_2_out);
  xor xor_1 (SignO, or_2_out, xor_2_out);
  or or_1 (or_1_out, and_1_out, and_3_out);
  // NoConnect on or_1_out
  and and_2 (out_13, clock_1_out, SignO);
  and and_3 (and_3_out, in_5, SignR);
  xor xor_2 (xor_2_out, in_5, SignR);
  and and_4 (and_4_out, or_4_out, xor_4_out);
  and and_5 (out_14, clock_1_out, xor_3_out);
  xor xor_3 (xor_3_out, or_4_out, xor_4_out);
  or or_2 (or_2_out, and_4_out, and_6_out);
  and and_6 (and_6_out, in_6, or_5_out);
  xor xor_4 (xor_4_out, in_6, or_5_out);
  not not_1 (not_1_out, Add_Sub_command);
  and and_7 (A, not_1_out, in_1);
  not not_2 (not_2_out, and_11_out);
  and and_8 (and_8_out, not_2_out, and_12_out);
  // NoConnect on and_8_out
  or or_3 (SignR, A, xor_5_out);
  and and_9 (and_9_out, and_20_out, xor_8_out);
  and and_10 (out_15, clock_1_out, xor_6_out);
  and and_11 (and_11_out, in_1, Add_Sub_command);
  and and_12 (and_12_out, not_4_out, and_17_out);
  xor xor_5 (xor_5_out, not_2_out, and_12_out);
  xor xor_6 (xor_6_out, and_20_out, xor_8_out);
  or or_4 (or_4_out, and_9_out, and_14_out);
  not not_3 (not_3_out, Add_Sub_command);
  and and_13 (B, not_3_out, in_2);
  not not_4 (not_4_out, and_15_out);
  xor xor_7 (xor_7_out, not_4_out, and_17_out);
  or or_5 (or_5_out, B, xor_7_out);
  and and_14 (and_14_out, in_7, or_6_out);
  xor xor_8 (xor_8_out, in_7, or_6_out);
  not not_5 (not_5_out, Add_Sub_command);
  and and_15 (and_15_out, in_2, Add_Sub_command);
  and and_16 (C, not_5_out, in_3);
  not not_6 (not_6_out, and_18_out);
  and and_17 (and_17_out, not_6_out, and_19_out);
  or or_6 (or_6_out, C, xor_9_out);
  and and_18 (and_18_out, in_3, Add_Sub_command);
  and and_19 (and_19_out, not_8_out, 1'b1);
  xor xor_9 (xor_9_out, not_6_out, and_19_out);
  and and_20 (and_20_out, in_8, or_7_out);
  xor xor_10 (xor_10_out, in_8, or_7_out);
  and and_21 (out_16, clock_1_out, xor_10_out);
  not not_7 (not_7_out, Add_Sub_command);
  and and_22 (D, not_7_out, in_4);
  not not_8 (not_8_out, and_23_out);
  xor xor_11 (xor_11_out, not_8_out, 1'b1);
  or or_7 (or_7_out, D, xor_11_out);
  and and_23 (and_23_out, in_4, Add_Sub_command);
  not not_9 (not_9_out, out_14);
  not not_10 (not_10_out, out_15);
  and and_24 (and_24_out, not_9_out, not_10_out, not_11_out);
  not not_11 (not_11_out, out_16);
  xor xor_12 (xor_12_out, in_5, SignO);
  xor xor_13 (xor_13_out, SignR, SignO);
  and and_25 (and_25_out, xor_12_out, xor_13_out);
  and and_26 (and_26_out, SignR, SignO, Add_Sub_command, and_24_out);
  not not_12 (not_12_out, SignO);
  not not_13 (not_13_out, xor_3_out);
  and and_27 (and_27_out, not_12_out, not_13_out, not_14_out, not_15_out);
  not not_14 (not_14_out, xor_6_out);
  not not_15 (not_15_out, xor_10_out);
  // NoConnect on clock_1_out
  or or_8 (or_8_out, and_25_out, and_26_out);
  and and_28 (out_10, SignO, clock_1_out);
  and and_29 (out_11, and_27_out, clock_1_out);
  and and_30 (out_12, or_8_out, clock_1_out);

  // Other names for the same wires on the sheet: SignL = in_5; Sub = Add_Sub_command

  // Notes on the sheet:
  //   Gwen Guan 260950108
  //   L input
  //   A-out output
  //   R input
  //   Negative
  //   Zero
  //   Overflow
endmodule
