// Logisim project a7.circ as structural Verilog: 19 circuits, main circuit main
module main (
  input  Reset,
  output Zero,
  output Negative,
  output Overflow
);

  wire addr_1_a1out, addr_1_a2out, addr_1_a3out, alu_1_a1, alu_1_a2, alu_1_a3, alu_1_a4, ALUmode, and_1_out,
       and_2_out, and_3_out, and_4_out, and_5_out, and_6_out, and_7_out, and_8_out, classicalram_1_d1out,
       classicalram_1_d2out, classicalram_1_d3out, classicalram_1_d4out, CLK, cu_1_add, cu_1_load, cu_1_save,
       cu_1_subhalt, integrationcircuit_1_a1, integrationcircuit_1_a2, integrationcircuit_1_a3,
       integrationcircuit_1_addrread, integrationcircuit_1_addrwrite, integrationcircuit_1_irwrite,
       integrationcircuit_1_len, integrationcircuit_1_lread, integrationcircuit_1_marwrite,
       integrationcircuit_1_mbrwrite, integrationcircuit_1_pcinc, integrationcircuit_1_pcread,
       integrationcircuit_1_r1en, integrationcircuit_1_r1write, integrationcircuit_1_r2en,
       integrationcircuit_1_r2write, integrationcircuit_1_ramwrite, integrationcircuit_1_ren,
       integrationcircuit_1_rread, ir_1_d1out, ir_1_d2out, ir_1_d3out, ir_1_d4out, left_1_d1out,
       left_1_d2out, left_1_d3out, left_1_d4out, mar_1_a1out, mar_1_a2out, mar_1_a3out, mbr_1_d1out,
       mbr_1_d2out, mbr_1_d3out, mbr_1_d4out, or_1_out, or_2_out, or_3_out, or_4_out, or_5_out, or_6_out,
       or_7_out, or_8_out, or_9_out, or_10_out, or_11_out, or_12_out, or_13_out, or_14_out, or_15_out,
       pc_1_a1out, pc_1_a2out, pc_1_a3out, r1_1_d1out, r1_1_d2out, r1_1_d3out, r1_1_d4out, r2_1_d1out,
       r2_1_d2out, r2_1_d3out, r2_1_d4out, RAMen, right_1_d1out, right_1_d2out, right_1_d3out, right_1_d4out;

  and and_1 (and_1_out, classicalram_1_d4out, RAMen);
  and and_2 (and_2_out, classicalram_1_d3out, RAMen);
  and and_3 (and_3_out, classicalram_1_d2out, RAMen);
  and and_4 (and_4_out, classicalram_1_d1out, RAMen);
  Clock clock_1 (.out(CLK));
  ClassicalRAM classicalram_1 (
    .D4out(classicalram_1_d4out), .D3out(classicalram_1_d3out), .D2out(classicalram_1_d2out),
    .D1out(classicalram_1_d1out), .CLK(CLK), .A1(mar_1_a1out), .Mode(integrationcircuit_1_ramwrite),
    .D4in(or_4_out), .D3in(or_5_out), .A3(mar_1_a3out), .D2in(or_6_out), .D1in(or_7_out), .A2(mar_1_a2out));
  or or_1 (or_1_out, pc_1_a1out, addr_1_a1out);
  or or_2 (or_2_out, pc_1_a2out, addr_1_a2out);
  or or_3 (or_3_out, pc_1_a3out, addr_1_a3out);
  MAR mar_1 (
    .MARwrite(integrationcircuit_1_marwrite), .Clk(CLK), .A1in(or_1_out), .A2in(or_2_out), .A3in(or_3_out),
    .A1out(mar_1_a1out), .A2out(mar_1_a2out), .A3out(mar_1_a3out));
  MBR mbr_1 (
    .MBRwrite(integrationcircuit_1_mbrwrite), .Clk(CLK), .D1in(and_4_out), .D2in(and_3_out),
    .D3in(and_2_out), .D4in(and_1_out), .D1out(mbr_1_d1out), .D2out(mbr_1_d2out), .D3out(mbr_1_d3out),
    .D4out(mbr_1_d4out));
  or or_4 (or_4_out, or_12_out, and_1_out);
  or or_5 (or_5_out, or_13_out, and_2_out);
  or or_6 (or_6_out, or_14_out, and_3_out);
  or or_7 (or_7_out, or_15_out, and_4_out);
  R1 r1_1 (
    .R1write(integrationcircuit_1_r1write), .Clk(CLK), .R1En(integrationcircuit_1_r1en), .D4in(or_4_out),
    .D3in(or_5_out), .D2in(or_6_out), .D1in(or_7_out), .D4out(r1_1_d4out), .D3out(r1_1_d3out),
    .D2out(r1_1_d2out), .D1out(r1_1_d1out));
  and and_5 (and_5_out, integrationcircuit_1_ren, right_1_d1out);
  Right right_1 (
    .D1out(right_1_d1out), .D2out(right_1_d2out), .D3out(right_1_d3out), .D4out(right_1_d4out),
    .D1in(or_7_out), .D2in(or_6_out), .D3in(or_5_out), .D4in(or_4_out), .Ren(integrationcircuit_1_ren),
    .Clk(CLK), .Rread(integrationcircuit_1_lread));
  Left left_1 (
    .D1out(left_1_d1out), .D2out(left_1_d2out), .D3out(left_1_d3out), .D4out(left_1_d4out), .D1in(or_7_out),
    .D2in(or_6_out), .D3in(or_5_out), .D4in(or_4_out), .Len(integrationcircuit_1_len), .Clk(CLK),
    .Lread(integrationcircuit_1_rread));
  PC pc_1 (
    .A1out(pc_1_a1out), .A3out(pc_1_a3out), .A2out(pc_1_a2out), .Clk(CLK), .Inc(integrationcircuit_1_pcinc),
    .Reset(Reset), .PCread(integrationcircuit_1_pcread));
  IR ir_1 (
    .IRwrite(integrationcircuit_1_irwrite), .Clk(CLK), .D1in(mbr_1_d1out), .D2in(mbr_1_d2out),
    .D3in(mbr_1_d3out), .D4in(mbr_1_d4out), .D1out(ir_1_d1out), .D2out(ir_1_d2out), .D3out(ir_1_d3out),
    .D4out(ir_1_d4out));
  and and_6 (and_6_out, integrationcircuit_1_ren, right_1_d2out);
  or or_8 (or_8_out, left_1_d1out, and_5_out);
  or or_9 (or_9_out, left_1_d2out, and_6_out);
  and and_7 (and_7_out, integrationcircuit_1_ren, right_1_d2out);
  and and_8 (and_8_out, integrationcircuit_1_ren, right_1_d3out);
  or or_10 (or_10_out, left_1_d3out, and_7_out);
  or or_11 (or_11_out, left_1_d4out, and_8_out);
  R2 r2_1 (
    .R2write(integrationcircuit_1_r2write), .Clk(CLK), .R2en(integrationcircuit_1_r2en), .D4in(or_4_out),
    .D3in(or_5_out), .D2in(or_6_out), .D1in(or_7_out), .D4out(r2_1_d4out), .D3out(r2_1_d3out),
    .D2out(r2_1_d2out), .D1out(r2_1_d1out));
  or or_12 (or_12_out, r1_1_d4out, alu_1_a4, r2_1_d4out);
  Addr addr_1 (
    .A1out(addr_1_a1out), .A2out(addr_1_a2out), .A3out(addr_1_a3out), .A1in(integrationcircuit_1_a1),
    .A2in(integrationcircuit_1_a2), .A3in(integrationcircuit_1_a3),
    .ADDRwrite(integrationcircuit_1_addrwrite), .Clk(CLK), .ADDRread(integrationcircuit_1_addrread));
  or or_13 (or_13_out, r1_1_d3out, alu_1_a3, r2_1_d3out);
  or or_14 (or_14_out, r1_1_d2out, alu_1_a2, r2_1_d2out);
  ALU alu_1 (
    .Zero(Zero), .Negative(Negative), .Overflow(Overflow), .A4(alu_1_a4), .A3(alu_1_a3), .A2(alu_1_a2),
    .A1(alu_1_a1), .Mode(ALUmode), .CLK(CLK), .L4(or_11_out), .L3(or_10_out), .L2(or_9_out), .L1(or_8_out),
    .R4(right_1_d4out), .R3(right_1_d3out), .R2(right_1_d2out), .R1(right_1_d1out));
  or or_15 (or_15_out, r1_1_d1out, alu_1_a1, r2_1_d1out);
  CU cu_1 (
    .IR1(ir_1_d4out), .IR2(ir_1_d3out), .CLK(CLK), .Load(cu_1_load), .Save(cu_1_save), .Add(cu_1_add),
    .SubHalt(cu_1_subhalt));
  IntegrationCircuit integrationcircuit_1 (
    .ADDRwrite(integrationcircuit_1_addrwrite), .R1write(integrationcircuit_1_r1write),
    .R2write(integrationcircuit_1_r2write), .ADDRread(integrationcircuit_1_addrread),
    .R1en(integrationcircuit_1_r1en), .R2en(integrationcircuit_1_r2en), .ALUmode(ALUmode), .RAMen(RAMen),
    .RAMwrite(integrationcircuit_1_ramwrite), .MARwrite(integrationcircuit_1_marwrite),
    .Len(integrationcircuit_1_len), .Ren(integrationcircuit_1_ren), .PCread(integrationcircuit_1_pcread),
    .Lread(integrationcircuit_1_lread), .Rread(integrationcircuit_1_rread),
    .MBRwrite(integrationcircuit_1_mbrwrite), .PCinc(integrationcircuit_1_pcinc),
    .IRwrite(integrationcircuit_1_irwrite), .A3(integrationcircuit_1_a3), .A2(integrationcircuit_1_a2),
    .A1(integrationcircuit_1_a1), .Reset(Reset), .Load(cu_1_load), .Save(cu_1_save), .Add(cu_1_add),
    .SubHalt(cu_1_subhalt), .IR3(ir_1_d2out), .IR4(ir_1_d1out), .CLK(CLK));

  // Notes on the sheet:
  //   Gwen Guan 260950108
  //   System Bus
  //   CPU Bus
  //   Please click Reset once (turn it on and then off) before using the clock to execute
endmodule

module ALU (
  input  L4,
  input  L3,
  input  L2,
  input  L1,
  input  R4,
  input  R3,
  input  R2,
  input  R1,
  input  CLK,
  input  Mode,
  output Zero,
  output Negative,
  output Overflow,
  output A4,
  output A3,
  output A2,
  output A1
);

  wire and_1_out, and_2_out, and_3_out, and_4_out, and_5_out, and_6_out, and_7_out, and_8_out, and_9_out,
       and_10_out, and_11_out, and_12_out, and_13_out, and_14_out, and_15_out, and_16_out, and_17_out,
       and_18_out, and_19_out, and_20_out, and_21_out, and_22_out, and_24_out, and_25_out, and_26_out,
       and_27_out, fulladder_1_c, fulladder_2_c, fulladder_3_c, Neg_out, not_1_out, not_2_out, not_3_out,
       not_4_out, not_5_out, not_6_out, not_7_out, not_8_out, not_9_out, not_10_out, not_11_out, not_12_out,
       not_13_out, not_14_out, not_15_out, or_1_out, or_2_out, or_3_out, or_4_out, or_5_out, Pos_out,
       xor_2_out, xor_3_out, xor_4_out, xor_5_out;

  not not_1 (not_1_out, Mode);
  and and_1 (and_1_out, L4, CLK);
  and and_2 (and_2_out, L3, CLK);
  and and_3 (and_3_out, L2, CLK);
  FullAdder fulladder_1 (.A(or_1_out), .B(and_1_out), .Carry(fulladder_2_c), .C(fulladder_1_c), .Sum(A4));
  and and_4 (and_4_out, L1, CLK);
  FullAdder fulladder_2 (.A(or_2_out), .B(and_2_out), .Carry(fulladder_3_c), .C(fulladder_2_c), .Sum(A3));
  or or_1 (or_1_out, xor_2_out, and_6_out);
  FullAdder fulladder_3 (.A(or_3_out), .B(and_3_out), .Carry(and_5_out), .C(fulladder_3_c), .Sum(A2));
  or or_2 (or_2_out, xor_3_out, and_8_out);
  or or_3 (or_3_out, xor_4_out, and_9_out);
  and and_5 (and_5_out, and_4_out, or_4_out);
  xor xor_1 (A1, and_4_out, or_4_out);
  and and_6 (and_6_out, and_12_out, not_1_out);
  and and_7 (and_7_out, not_6_out, and_10_out);
  or or_4 (or_4_out, xor_5_out, and_14_out);
  not not_2 (not_2_out, A1);
  not not_3 (not_3_out, A2);
  not not_4 (not_4_out, A3);
  not not_5 (not_5_out, A4);
  and and_8 (and_8_out, and_13_out, not_1_out);
  and and_9 (and_9_out, and_17_out, not_1_out);
  xor xor_2 (xor_2_out, not_6_out, and_10_out);
  and and_10 (and_10_out, not_10_out, and_16_out);
  and and_11 (and_11_out, not_2_out, not_3_out, not_4_out, not_5_out);
  and and_12 (and_12_out, R4, CLK);
  and and_13 (and_13_out, R3, CLK);
  and and_14 (and_14_out, and_18_out, not_1_out);
  and and_15 (and_15_out, and_12_out, Mode);
  not not_6 (not_6_out, and_15_out);
  xor xor_3 (xor_3_out, not_10_out, and_16_out);
  and and_16 (and_16_out, not_11_out, and_22_out);
  not not_7 (not_7_out, or_1_out);
  not not_8 (not_8_out, and_1_out);
  not not_9 (not_9_out, or_1_out);
  and and_17 (and_17_out, R2, CLK);
  and and_18 (and_18_out, R1, CLK);
  and and_19 (and_19_out, and_13_out, Mode);
  and and_20 (and_20_out, and_17_out, Mode);
  and and_21 (and_21_out, and_18_out, Mode);
  not not_10 (not_10_out, and_19_out);
  not not_11 (not_11_out, and_20_out);
  not not_12 (not_12_out, and_21_out);
  xor xor_4 (xor_4_out, not_11_out, and_22_out);
  and and_22 (and_22_out, not_12_out, 1'b1);
  and Neg (Neg_out, or_1_out, and_1_out);
  and Pos (Pos_out, not_7_out, not_8_out);
  and and_23 (Zero, and_11_out, CLK);
  xor xor_5 (xor_5_out, not_12_out, 1'b1);
  and and_24 (and_24_out, A4, Neg_out);
  and and_25 (and_25_out, Pos_out, A4);
  and and_26 (and_26_out, not_13_out, not_9_out, fulladder_1_c);
  not not_13 (not_13_out, Mode);
  not not_14 (not_14_out, fulladder_1_c);
  and and_27 (and_27_out, and_24_out, not_14_out);
  or or_5 (or_5_out, and_26_out, and_25_out, and_27_out);
  not not_15 (not_15_out, Zero);
  and notZero (Overflow, or_5_out, not_15_out);

  assign Negative = A4;

  // Other names for the same wires on the sheet: Clock = CLK; CMD = Mode

  // Notes on the sheet:
  //   Add/Sub command
  //   0 add, 1 sub
  //   B Input
  //   L input
  //   A-out output
  //   A Input
  //   Adder
  //   R Input
  //   2's Complement
  //   Status output
  //   -8 + -8 is underflow (not supported)
endmodule

module FullAdder (
  input  A,
  input  B,
  input  Carry,
  output C,
  output Sum
);

  wire and_1_out, and_2_out, xor_1_out;

  and and_1 (and_1_out, A, B);
  xor xor_1 (xor_1_out, A, B);
  and and_2 (and_2_out, xor_1_out, Carry);
  or or_1 (C, and_1_out, and_2_out);
  xor xor_2 (Sum, xor_1_out, Carry);
endmodule

module ClassicalRAM (
  input  CLK,
  input  A3,
  input  A2,
  input  A1,
  input  Mode,
  input  D4in,
  input  D3in,
  input  D2in,
  input  D1in,
  output D4out,
  output D3out,
  output D2out,
  output D1out
);

  wire and_1_out, and_2_out, and_3_out, and_4_out, and_5_out, and_6_out, and_7_out, and_8_out, and_9_out,
       and_10_out, and_11_out, and_12_out, and_13_out, and_14_out, and_15_out, and_16_out, and_17_out,
       and_18_out, and_19_out, and_20_out, and_21_out, and_22_out, and_23_out, and_24_out, and_25_out,
       and_26_out, and_27_out, and_28_out, and_29_out, and_30_out, and_31_out, and_32_out, and_33_out,
       and_34_out, and_35_out, and_36_out, and_37_out, and_38_out, and_39_out, and_40_out, and_41_out,
       and_42_out, and_43_out, and_44_out, and_45_out, and_46_out, and_47_out, and_48_out, and_49_out,
       and_50_out, and_51_out, and_52_out, and_53_out, and_54_out, and_55_out, and_56_out, and_57_out,
       and_58_out, and_59_out, and_60_out, and_61_out, and_62_out, and_63_out, and_64_out, and_65_out,
       and_66_out, and_67_out, and_68_out, and_69_out, and_70_out, and_71_out, and_72_out, and_73_out,
       and_74_out, and_75_out, and_76_out, and_77_out, and_78_out, and_79_out, and_80_out, d_ff_1_q,
       d_ff_2_q, d_ff_3_q, d_ff_4_q, d_ff_5_q, d_ff_6_q, d_ff_7_q, d_ff_8_q, d_ff_9_q, d_ff_10_q, d_ff_11_q,
       d_ff_12_q, d_ff_13_q, d_ff_14_q, d_ff_15_q, d_ff_16_q, d_ff_17_q, d_ff_18_q, d_ff_19_q, d_ff_20_q,
       d_ff_21_q, d_ff_22_q, d_ff_23_q, d_ff_24_q, d_ff_25_q, d_ff_26_q, d_ff_27_q, d_ff_28_q, d_ff_29_q,
       d_ff_30_q, d_ff_31_q, d_ff_32_q, not_1_out, not_2_out, not_3_out, not_4_out, not_5_out, not_6_out,
       not_7_out, not_8_out, not_9_out, not_10_out, not_11_out, not_12_out, not_13_out;

  not not_1 (not_1_out, A1);
  not not_2 (not_2_out, A2);
  not not_3 (not_3_out, A2);
  not not_4 (not_4_out, A1);
  not not_5 (not_5_out, A3);
  not not_6 (not_6_out, A3);
  not not_7 (not_7_out, A1);
  not not_8 (not_8_out, A3);
  not not_9 (not_9_out, A2);
  not not_10 (not_10_out, A3);
  not not_11 (not_11_out, A2);
  not not_12 (not_12_out, A1);
  and and_1 (and_1_out, A3, A2, CLK, A1);
  and and_2 (and_2_out, and_1_out, Mode);
  and and_3 (and_3_out, A3, A2, CLK, not_1_out);
  and and_4 (and_4_out, and_3_out, Mode);
  and and_5 (and_5_out, A3, not_2_out, CLK, A1);
  and and_6 (and_6_out, and_5_out, Mode);
  and and_7 (and_7_out, A3, not_3_out, CLK, not_4_out);
  and and_8 (and_8_out, and_7_out, Mode);
  and and_9 (and_9_out, not_5_out, A2, CLK, A1);
  and and_10 (and_10_out, and_9_out, Mode);
  and and_11 (and_11_out, not_6_out, A2, CLK, not_7_out);
  and and_12 (and_12_out, and_11_out, Mode);
  and and_13 (and_13_out, not_8_out, not_9_out, CLK, A1);
  and and_14 (and_14_out, and_13_out, Mode);
  and and_15 (and_15_out, not_10_out, CLK, not_11_out, not_12_out);
  and and_16 (and_16_out, and_15_out, Mode);
  and and_17 (and_17_out, and_1_out, Mode, D4in);
  D_Flip_Flop #(.trigger("high")) d_ff_1 (.D(and_17_out), .clk(and_2_out), .Q(d_ff_1_q));  // open: Qn, preset, reset
  and and_18 (and_18_out, and_3_out, Mode, D4in);
  D_Flip_Flop #(.trigger("high")) d_ff_2 (.D(and_18_out), .clk(and_4_out), .Q(d_ff_2_q));  // open: Qn, preset, reset
  and and_19 (and_19_out, and_5_out, Mode, D4in);
  D_Flip_Flop #(.trigger("high")) d_ff_3 (.D(and_19_out), .clk(and_6_out), .Q(d_ff_3_q));  // open: Qn, preset, reset
  and and_20 (and_20_out, and_7_out, Mode, D4in);
  D_Flip_Flop #(.trigger("high")) d_ff_4 (.D(and_20_out), .clk(and_8_out), .Q(d_ff_4_q));  // open: Qn, preset, reset
  and and_21 (and_21_out, and_9_out, Mode, D4in);
  D_Flip_Flop #(.trigger("high")) d_ff_5 (.D(and_21_out), .clk(and_10_out), .Q(d_ff_5_q));  // open: Qn, preset, reset
  and and_22 (and_22_out, and_11_out, Mode, D4in);
  D_Flip_Flop #(.trigger("high")) d_ff_6 (.D(and_22_out), .clk(and_12_out), .Q(d_ff_6_q));  // open: Qn, preset, reset
  and and_23 (and_23_out, and_13_out, Mode, D4in);
  D_Flip_Flop #(.trigger("high")) d_ff_7 (.D(and_23_out), .clk(and_14_out), .Q(d_ff_7_q));  // open: Qn, preset, reset
  and and_24 (and_24_out, and_15_out, Mode, D4in);
  D_Flip_Flop #(.trigger("high")) d_ff_8 (.D(and_24_out), .clk(and_16_out), .Q(d_ff_8_q));  // open: Qn, preset, reset
  not not_13 (not_13_out, Mode);
  or or_1 (D4out, and_25_out, and_26_out, and_27_out, and_28_out, and_29_out, and_30_out, and_31_out, and_32_out);
  and and_25 (and_25_out, d_ff_1_q, and_1_out, not_13_out);
  and and_26 (and_26_out, d_ff_2_q, and_3_out, not_13_out);
  and and_27 (and_27_out, d_ff_3_q, and_5_out, not_13_out);
  and and_28 (and_28_out, d_ff_4_q, and_7_out, not_13_out);
  and and_29 (and_29_out, d_ff_5_q, and_9_out, not_13_out);
  and and_30 (and_30_out, d_ff_6_q, and_11_out, not_13_out);
  and and_31 (and_31_out, d_ff_7_q, and_13_out, not_13_out);
  and and_32 (and_32_out, d_ff_8_q, and_15_out, not_13_out);
  and and_33 (and_33_out, and_1_out, Mode, D3in);
  D_Flip_Flop #(.trigger("high")) d_ff_9 (.D(and_33_out), .clk(and_2_out), .Q(d_ff_9_q));  // open: Qn, preset, reset
  and and_34 (and_34_out, and_3_out, Mode, D3in);
  D_Flip_Flop #(.trigger("high")) d_ff_10 (.D(and_34_out), .clk(and_4_out), .Q(d_ff_10_q));  // open: Qn, preset, reset
  and and_35 (and_35_out, and_5_out, Mode, D3in);
  D_Flip_Flop #(.trigger("high")) d_ff_11 (.D(and_35_out), .clk(and_6_out), .Q(d_ff_11_q));  // open: Qn, preset, reset
  and and_36 (and_36_out, and_7_out, Mode, D3in);
  D_Flip_Flop #(.trigger("high")) d_ff_12 (.D(and_36_out), .clk(and_8_out), .Q(d_ff_12_q));  // open: Qn, preset, reset
  and and_37 (and_37_out, and_9_out, Mode, D3in);
  D_Flip_Flop #(.trigger("high")) d_ff_13 (.D(and_37_out), .clk(and_10_out), .Q(d_ff_13_q));  // open: Qn, preset, reset
  and and_38 (and_38_out, and_11_out, Mode, D3in);
  D_Flip_Flop #(.trigger("high")) d_ff_14 (.D(and_38_out), .clk(and_12_out), .Q(d_ff_14_q));  // open: Qn, preset, reset
  and and_39 (and_39_out, and_13_out, Mode, D3in);
  D_Flip_Flop #(.trigger("high")) d_ff_15 (.D(and_39_out), .clk(and_14_out), .Q(d_ff_15_q));  // open: Qn, preset, reset
  and and_40 (and_40_out, and_15_out, Mode, D3in);
  D_Flip_Flop #(.trigger("high")) d_ff_16 (.D(and_40_out), .clk(and_16_out), .Q(d_ff_16_q));  // open: Qn, preset, reset
  or or_2 (D3out, and_41_out, and_42_out, and_43_out, and_44_out, and_45_out, and_46_out, and_47_out, and_48_out);
  and and_41 (and_41_out, d_ff_9_q, and_1_out, not_13_out);
  and and_42 (and_42_out, d_ff_10_q, and_3_out, not_13_out);
  and and_43 (and_43_out, d_ff_11_q, and_5_out, not_13_out);
  and and_44 (and_44_out, d_ff_12_q, and_7_out, not_13_out);
  and and_45 (and_45_out, d_ff_13_q, and_9_out, not_13_out);
  and and_46 (and_46_out, d_ff_14_q, and_11_out, not_13_out);
  and and_47 (and_47_out, d_ff_15_q, and_13_out, not_13_out);
  and and_48 (and_48_out, d_ff_16_q, and_15_out, not_13_out);
  Clock clock_1 ();  // open: out
  and and_49 (and_49_out, and_1_out, Mode, D2in);
  and and_50 (and_50_out, and_3_out, Mode, D2in);
  and and_51 (and_51_out, and_5_out, Mode, D2in);
  and and_52 (and_52_out, and_7_out, Mode, D2in);
  and and_53 (and_53_out, and_9_out, Mode, D2in);
  and and_54 (and_54_out, and_11_out, Mode, D2in);
  and and_55 (and_55_out, and_13_out, Mode, D2in);
  and and_56 (and_56_out, and_15_out, Mode, D2in);
  D_Flip_Flop #(.trigger("high")) d_ff_17 (.D(and_49_out), .clk(and_2_out), .Q(d_ff_17_q));  // open: Qn, preset, reset
  D_Flip_Flop #(.trigger("high")) d_ff_18 (.D(and_50_out), .clk(and_4_out), .Q(d_ff_18_q));  // open: Qn, preset, reset
  D_Flip_Flop #(.trigger("high")) d_ff_19 (.D(and_51_out), .clk(and_6_out), .Q(d_ff_19_q));  // open: Qn, preset, reset
  D_Flip_Flop #(.trigger("high")) d_ff_20 (.D(and_52_out), .clk(and_8_out), .Q(d_ff_20_q));  // open: Qn, preset, reset
  D_Flip_Flop #(.trigger("high")) d_ff_21 (.D(and_53_out), .clk(and_10_out), .Q(d_ff_21_q));  // open: Qn, preset, reset
  D_Flip_Flop #(.trigger("high")) d_ff_22 (.D(and_54_out), .clk(and_12_out), .Q(d_ff_22_q));  // open: Qn, preset, reset
  D_Flip_Flop #(.trigger("high")) d_ff_23 (.D(and_55_out), .clk(and_14_out), .Q(d_ff_23_q));  // open: Qn, preset, reset
  D_Flip_Flop #(.trigger("high")) d_ff_24 (.D(and_56_out), .clk(and_16_out), .Q(d_ff_24_q));  // open: Qn, preset, reset
  or or_3 (D2out, and_57_out, and_58_out, and_59_out, and_60_out, and_61_out, and_62_out, and_63_out, and_64_out);
  and and_57 (and_57_out, d_ff_17_q, and_1_out, not_13_out);
  and and_58 (and_58_out, d_ff_18_q, and_3_out, not_13_out);
  and and_59 (and_59_out, d_ff_19_q, and_5_out, not_13_out);
  and and_60 (and_60_out, d_ff_20_q, and_7_out, not_13_out);
  and and_61 (and_61_out, d_ff_21_q, and_9_out, not_13_out);
  and and_62 (and_62_out, d_ff_22_q, and_11_out, not_13_out);
  and and_63 (and_63_out, d_ff_23_q, and_13_out, not_13_out);
  and and_64 (and_64_out, d_ff_24_q, and_15_out, not_13_out);
  and and_65 (and_65_out, and_1_out, Mode, D1in);
  D_Flip_Flop #(.trigger("high")) d_ff_25 (.D(and_65_out), .clk(and_2_out), .Q(d_ff_25_q));  // open: Qn, preset, reset
  and and_66 (and_66_out, and_3_out, Mode, D1in);
  D_Flip_Flop #(.trigger("high")) d_ff_26 (.D(and_66_out), .clk(and_4_out), .Q(d_ff_26_q));  // open: Qn, preset, reset
  and and_67 (and_67_out, and_5_out, Mode, D1in);
  D_Flip_Flop #(.trigger("high")) d_ff_27 (.D(and_67_out), .clk(and_6_out), .Q(d_ff_27_q));  // open: Qn, preset, reset
  and and_68 (and_68_out, and_7_out, Mode, D1in);
  D_Flip_Flop #(.trigger("high")) d_ff_28 (.D(and_68_out), .clk(and_8_out), .Q(d_ff_28_q));  // open: Qn, preset, reset
  and and_69 (and_69_out, and_9_out, Mode, D1in);
  D_Flip_Flop #(.trigger("high")) d_ff_29 (.D(and_69_out), .clk(and_10_out), .Q(d_ff_29_q));  // open: Qn, preset, reset
  and and_70 (and_70_out, and_11_out, Mode, D1in);
  D_Flip_Flop #(.trigger("high")) d_ff_30 (.D(and_70_out), .clk(and_12_out), .Q(d_ff_30_q));  // open: Qn, preset, reset
  and and_71 (and_71_out, and_13_out, Mode, D1in);
  D_Flip_Flop #(.trigger("high")) d_ff_31 (.D(and_71_out), .clk(and_14_out), .Q(d_ff_31_q));  // open: Qn, preset, reset
  and and_72 (and_72_out, and_15_out, Mode, D1in);
  D_Flip_Flop #(.trigger("high")) d_ff_32 (.D(and_72_out), .clk(and_16_out), .Q(d_ff_32_q));  // open: Qn, preset, reset
  or or_4 (D1out, and_73_out, and_74_out, and_75_out, and_76_out, and_77_out, and_78_out, and_79_out, and_80_out);
  and and_73 (and_73_out, d_ff_25_q, and_1_out, not_13_out);
  and and_74 (and_74_out, d_ff_26_q, and_3_out, not_13_out);
  and and_75 (and_75_out, d_ff_27_q, and_5_out, not_13_out);
  and and_76 (and_76_out, d_ff_28_q, and_7_out, not_13_out);
  and and_77 (and_77_out, d_ff_29_q, and_9_out, not_13_out);
  and and_78 (and_78_out, d_ff_30_q, and_11_out, not_13_out);
  and and_79 (and_79_out, d_ff_31_q, and_13_out, not_13_out);
  and and_80 (and_80_out, d_ff_32_q, and_15_out, not_13_out);

  // Notes on the sheet:
  //   3-bit address input pins
  //   Mode input pin
  //   4-bit data input pins
  //   4-bit data output pins
endmodule

module CU (
  input  IR1,
  input  IR2,
  input  CLK,
  output Load,
  output Save,
  output Add,
  output SubHalt
);

  wire not_1_out, not_2_out, not_3_out, not_4_out;

  not not_1 (not_1_out, IR1);
  not not_2 (not_2_out, IR2);
  not not_3 (not_3_out, IR1);
  not not_4 (not_4_out, IR2);
  and and_1 (Load, not_1_out, CLK, not_2_out);
  and and_2 (Save, not_3_out, CLK, IR2);
  and and_3 (Add, IR1, CLK, not_4_out);
  and and_4 (SubHalt, IR1, IR2);
endmodule

module IntegrationCircuit (
  input  CLK,
  input  Reset,
  input  Load,
  input  Save,
  input  Add,
  input  SubHalt,
  input  IR3,
  input  IR4,
  output A3,
  output A2,
  output A1,
  output PCinc,
  output MBRwrite,
  output IRwrite,
  output R1write,
  output R2write,
  output R1en,
  output R2en,
  output RAMen,
  output RAMwrite,
  output MARwrite,
  output ALUmode,
  output Len,
  output Ren,
  output PCread,
  output Lread,
  output Rread,
  output ADDRwrite,
  output ADDRread
);

  wire and_2_out, and_3_out, and_4_out, and_6_out, and_7_out, and_8_out, and_9_out, and_10_out, and_11_out,
       and_12_out, and_13_out, and_14_out, and_15_out, and_16_out, and_17_out, and_18_out, and_19_out,
       fetch_1_irwrite, fetch_1_marwrite, fetch_1_mbrwrite, fetch_1_pcinc, fetch_1_ramread, HALT, not_1_out,
       not_2_out, not_3_out, or_1_out, or_3_out, Step4, Step5, Step6, stepcounter_1_step1,
       stepcounter_1_step2, stepcounter_1_step3;

  and and_1 (HALT, SubHalt, IR3, IR4);
  and and_2 (and_2_out, CLK, ~HALT);  // AND_Gate
  or or_1 (or_1_out, Add, SubHalt);
  and and_3 (and_3_out, or_1_out, Step4);
  and and_4 (and_4_out, or_1_out, Step5);
  and and_5 (Lread, or_1_out, Step6);
  and and_6 (and_6_out, Load, Step4);
  and and_7 (and_7_out, Load, Step5);
  and and_8 (and_8_out, Load, Step6);
  and and_9 (and_9_out, Save, Step6);
  and and_10 (and_10_out, Save, Step4);
  and and_11 (and_11_out, Save, Step5);
  StepCounter stepcounter_1 (
    .CLK(and_2_out), .Reset(Reset), .Step1(stepcounter_1_step1), .Step2(stepcounter_1_step2),
    .Step3(stepcounter_1_step3), .Step4(Step4), .Step5(Step5), .Step6(Step6));
  not not_1 (not_1_out, IR3);
  not not_2 (not_2_out, IR3);
  not not_3 (not_3_out, IR3);
  or or_2 (ADDRwrite, and_6_out, and_10_out);
  and and_12 (and_12_out, and_8_out, IR3);
  and and_13 (and_13_out, and_8_out, not_1_out);
  and and_14 (and_14_out, and_9_out, IR3);
  and and_15 (and_15_out, and_9_out, not_2_out);
  and and_16 (and_16_out, and_4_out, IR3);
  and and_17 (and_17_out, and_4_out, not_3_out);
  or or_3 (or_3_out, stepcounter_1_step1, stepcounter_1_step3, stepcounter_1_step2);
  and and_18 (and_18_out, or_3_out, ~HALT);  // AND_Gate
  Fetch fetch_1 (
    .CLK(and_2_out), .Reset(Reset), .FetchEnable(and_18_out), .MARwrite(fetch_1_marwrite),
    .PCinc(fetch_1_pcinc), .PCread(PCread), .RAMread(fetch_1_ramread), .MBRwrite(fetch_1_mbrwrite),
    .IRwrite(fetch_1_irwrite));
  or or_4 (R1write, and_13_out, Lread);
  buf or_5 (R2write, and_12_out);  // OR_Gate
  or or_6 (R1en, and_15_out, and_3_out, and_17_out);
  or or_7 (R2en, and_14_out, and_16_out);
  or or_8 (RAMen, fetch_1_ramread, and_8_out);
  or or_9 (RAMwrite, and_15_out, and_14_out);
  or or_10 (MARwrite, and_7_out, fetch_1_marwrite, and_11_out);
  and and_19 (and_19_out, SubHalt, ~HALT);  // AND_Gate
  buf or_11 (ALUmode, and_19_out);  // OR_Gate
  buf or_12 (Len, and_3_out);  // OR_Gate
  or or_13 (Ren, and_16_out, and_17_out);
  or or_14 (ADDRread, and_11_out, and_7_out);
  buf or_15 (PCinc, fetch_1_pcinc);  // OR_Gate
  buf or_16 (MBRwrite, fetch_1_mbrwrite);  // OR_Gate
  buf or_17 (IRwrite, fetch_1_irwrite);  // OR_Gate

  assign A1 = IR4;
  assign A2 = 1'b0;
  assign A3 = 1'b0;
  assign Rread = Lread;

  // Notes on the sheet:
  //   SAVE
  //   LOAD
  //   ADD
endmodule

module R1 (
  input  R1write,
  input  Clk,
  input  R1En,
  input  D4in,
  input  D3in,
  input  D2in,
  input  D1in,
  output D4out,
  output D3out,
  output D2out,
  output D1out
);

  wire and_1_out, d_ff_1_q, d_ff_2_q, d_ff_3_q, d_ff_4_q, undriven;

  and and_1 (and_1_out, R1write, Clk);
  D_Flip_Flop #(.trigger("falling")) d_ff_1 (.D(D4in), .clk(and_1_out), .Q(d_ff_1_q));  // open: Qn, preset, reset
  D_Flip_Flop #(.trigger("falling")) d_ff_2 (
    .D(D3in), .clk(and_1_out), .Q(d_ff_2_q), .reset(undriven));  // open: Qn, preset
  D_Flip_Flop #(.trigger("falling")) d_ff_3 (.D(D2in), .clk(and_1_out), .Q(d_ff_3_q));  // open: Qn, preset, reset
  D_Flip_Flop #(.trigger("falling")) d_ff_4 (.D(D1in), .clk(and_1_out), .Q(d_ff_4_q));  // open: Qn, preset, reset
  and and_2 (D4out, R1En, d_ff_1_q);
  and and_3 (D3out, R1En, d_ff_2_q);
  and and_4 (D2out, R1En, d_ff_3_q);
  and and_5 (D1out, R1En, d_ff_4_q);
endmodule

module R2 (
  input  R2write,
  input  Clk,
  input  R2en,
  input  D4in,
  input  D3in,
  input  D2in,
  input  D1in,
  output D4out,
  output D3out,
  output D2out,
  output D1out
);

  wire and_1_out, d_ff_1_q, d_ff_2_q, d_ff_3_q, d_ff_4_q, undriven;

  and and_1 (and_1_out, R2write, Clk);
  D_Flip_Flop #(.trigger("falling")) d_ff_1 (.D(D4in), .clk(and_1_out), .Q(d_ff_1_q));  // open: Qn, preset, reset
  D_Flip_Flop #(.trigger("falling")) d_ff_2 (
    .D(D3in), .clk(and_1_out), .Q(d_ff_2_q), .reset(undriven));  // open: Qn, preset
  D_Flip_Flop #(.trigger("falling")) d_ff_3 (.D(D2in), .clk(and_1_out), .Q(d_ff_3_q));  // open: Qn, preset, reset
  D_Flip_Flop #(.trigger("falling")) d_ff_4 (.D(D1in), .clk(and_1_out), .Q(d_ff_4_q));  // open: Qn, preset, reset
  and and_2 (D4out, R2en, d_ff_1_q);
  and and_3 (D3out, R2en, d_ff_2_q);
  and and_4 (D2out, R2en, d_ff_3_q);
  and and_5 (D1out, R2en, d_ff_4_q);
endmodule

module IR (
  input  IRwrite,
  input  Clk,
  input  D1in,
  input  D2in,
  input  D3in,
  input  D4in,
  output D1out,
  output D2out,
  output D3out,
  output D4out
);

  wire and_1_out, undriven;

  and and_1 (and_1_out, IRwrite, Clk);
  D_Flip_Flop #(.trigger("falling")) d_ff_1 (.D(D1in), .clk(and_1_out), .Q(D1out));  // open: Qn, preset, reset
  D_Flip_Flop #(.trigger("falling")) d_ff_2 (
    .D(D2in), .clk(and_1_out), .Q(D2out), .reset(undriven));  // open: Qn, preset
  D_Flip_Flop #(.trigger("falling")) d_ff_3 (.D(D3in), .clk(and_1_out), .Q(D3out));  // open: Qn, preset, reset
  D_Flip_Flop #(.trigger("falling")) d_ff_4 (.D(D4in), .clk(and_1_out), .Q(D4out));  // open: Qn, preset, reset
endmodule

module MAR (
  input  MARwrite,
  input  Clk,
  input  A1in,
  input  A2in,
  input  A3in,
  output A1out,
  output A2out,
  output A3out
);

  wire and_1_out, d_ff_1_q, d_ff_2_q, d_ff_3_q, not_1_out, undriven;

  and and_1 (and_1_out, MARwrite, Clk);
  not not_1 (not_1_out, MARwrite);
  D_Flip_Flop #(.trigger("falling")) d_ff_1 (.D(A1in), .clk(and_1_out), .Q(d_ff_1_q));  // open: Qn, preset, reset
  D_Flip_Flop #(.trigger("falling")) d_ff_2 (
    .D(A2in), .clk(and_1_out), .Q(d_ff_2_q), .reset(undriven));  // open: Qn, preset
  D_Flip_Flop #(.trigger("falling")) d_ff_3 (.D(A3in), .clk(and_1_out), .Q(d_ff_3_q));  // open: Qn, preset, reset
  and and_2 (A1out, d_ff_1_q, not_1_out);
  and and_3 (A2out, d_ff_2_q, not_1_out);
  and and_4 (A3out, d_ff_3_q, not_1_out);
endmodule

module MBR (
  input  MBRwrite,
  input  Clk,
  input  D1in,
  input  D2in,
  input  D3in,
  input  D4in,
  output D1out,
  output D2out,
  output D3out,
  output D4out
);

  wire and_1_out, d_ff_1_q, d_ff_2_q, d_ff_3_q, d_ff_4_q, undriven;

  and and_1 (and_1_out, MBRwrite, Clk);
  D_Flip_Flop #(.trigger("falling")) d_ff_1 (.D(D1in), .clk(and_1_out), .Q(d_ff_1_q));  // open: Qn, preset, reset
  D_Flip_Flop #(.trigger("falling")) d_ff_2 (
    .D(D2in), .clk(and_1_out), .Q(d_ff_2_q), .reset(undriven));  // open: Qn, preset
  D_Flip_Flop #(.trigger("falling")) d_ff_3 (.D(D3in), .clk(and_1_out), .Q(d_ff_3_q));  // open: Qn, preset, reset
  D_Flip_Flop #(.trigger("falling")) d_ff_4 (.D(D4in), .clk(and_1_out), .Q(d_ff_4_q));  // open: Qn, preset, reset
  and and_2 (D1out, ~MBRwrite, d_ff_1_q);  // AND_Gate
  and and_3 (D2out, ~MBRwrite, d_ff_2_q);  // AND_Gate
  and and_4 (D3out, ~MBRwrite, d_ff_3_q);  // AND_Gate
  and and_5 (D4out, ~MBRwrite, d_ff_4_q);  // AND_Gate
endmodule

module PC (
  input  Clk,
  input  Reset,
  input  PCread,
  input  Inc,
  output A3out,
  output A2out,
  output A1out
);

  wire and_1_out, and_2_out, and_3_out, and_4_out, d_ff_1_q, d_ff_2_q, d_ff_3_q, undriven, undriven_2,
       xor_1_out, xor_2_out, xor_3_out;

  and and_1 (and_1_out, d_ff_1_q, and_2_out);
  xor xor_1 (xor_1_out, d_ff_1_q, and_2_out);
  and and_2 (and_2_out, d_ff_2_q, and_3_out);
  xor xor_2 (xor_2_out, d_ff_2_q, and_3_out);
  and and_3 (and_3_out, d_ff_3_q, 1'b1);
  xor xor_3 (xor_3_out, d_ff_3_q, 1'b1);
  and and_4 (and_4_out, Clk, Inc);
  D_Flip_Flop d_ff_1 (.D(xor_1_out), .clk(and_4_out), .Q(d_ff_1_q), .reset(Reset));  // open: Qn, preset
  D_Flip_Flop d_ff_2 (.D(xor_2_out), .clk(and_4_out), .Q(d_ff_2_q), .preset(undriven), .reset(Reset));  // open: Qn
  D_Flip_Flop d_ff_3 (.D(xor_3_out), .clk(and_4_out), .Q(d_ff_3_q), .preset(Reset), .reset(undriven_2));  // open: Qn
  and and_5 (A3out, d_ff_1_q, PCread);
  and and_6 (A2out, d_ff_2_q, PCread);
  and and_7 (A1out, d_ff_3_q, PCread);
endmodule

module Incrementer (
  input  D3,
  input  D2,
  input  D1,
  output S3,
  output S2,
  output S1
);

  wire and_1_out, and_2_out, and_3_out;

  and and_1 (and_1_out, D3, and_2_out);
  xor xor_1 (S3, D3, and_2_out);
  and and_2 (and_2_out, D2, and_3_out);
  xor xor_2 (S2, D2, and_3_out);
  and and_3 (and_3_out, D1, 1'b1);
  xor xor_3 (S1, D1, 1'b1);
endmodule

module StepCounter (
  input  CLK,
  input  Reset,
  output Step1,
  output Step2,
  output Step3,
  output Step4,
  output Step5,
  output Step6
);

  wire and_1_out, or_1_out, or_2_out, or_3_out, or_4_out, or_5_out, or_6_out;

  or or_1 (or_1_out, Step6, Step1);
  and and_1 (and_1_out, CLK, ~1'b0);  // AND_Gate
  or or_2 (or_2_out, Step1, Step2);
  T_Flip_Flop #(.trigger("falling")) t_ff_1 (
    .T(or_1_out), .clk(and_1_out), .Q(Step1), .preset(Reset));  // open: Qn, reset
  or or_3 (or_3_out, Step2, Step3);
  T_Flip_Flop #(.trigger("falling")) t_ff_2 (
    .T(or_2_out), .clk(and_1_out), .Q(Step2), .reset(Reset));  // open: Qn, preset
  or or_4 (or_4_out, Step3, Step4);
  T_Flip_Flop #(.trigger("falling")) t_ff_3 (
    .T(or_3_out), .clk(and_1_out), .Q(Step3), .reset(Reset));  // open: Qn, preset
  or or_5 (or_5_out, Step4, Step5);
  T_Flip_Flop #(.trigger("falling")) t_ff_4 (
    .T(or_4_out), .clk(and_1_out), .Q(Step4), .reset(Reset));  // open: Qn, preset
  or or_6 (or_6_out, Step5, Step6);
  T_Flip_Flop #(.trigger("falling")) t_ff_5 (
    .T(or_5_out), .clk(and_1_out), .Q(Step5), .reset(Reset));  // open: Qn, preset
  T_Flip_Flop #(.trigger("falling")) t_ff_6 (
    .T(or_6_out), .clk(and_1_out), .Q(Step6), .reset(Reset));  // open: Qn, preset
endmodule

module Addr (
  input  ADDRwrite,
  input  Clk,
  input  ADDRread,
  input  A1in,
  input  A2in,
  input  A3in,
  output A1out,
  output A2out,
  output A3out
);

  wire and_1_out, d_ff_1_q, d_ff_2_q, d_ff_3_q, undriven;

  and and_1 (and_1_out, ADDRwrite, Clk);
  D_Flip_Flop #(.trigger("falling")) d_ff_1 (.D(A1in), .clk(and_1_out), .Q(d_ff_1_q));  // open: Qn, preset, reset
  D_Flip_Flop #(.trigger("falling")) d_ff_2 (
    .D(A2in), .clk(and_1_out), .Q(d_ff_2_q), .reset(undriven));  // open: Qn, preset
  D_Flip_Flop #(.trigger("falling")) d_ff_3 (.D(A3in), .clk(and_1_out), .Q(d_ff_3_q));  // open: Qn, preset, reset
  and and_2 (A1out, d_ff_1_q, ADDRread);
  and and_3 (A2out, d_ff_2_q, ADDRread);
  and and_4 (A3out, d_ff_3_q, ADDRread);
endmodule

module Fetch (
  input  CLK,
  input  Reset,
  input  FetchEnable,
  output MARwrite,
  output PCinc,
  output PCread,
  output RAMread,
  output MBRwrite,
  output IRwrite
);

  wire fetchcounter_1_step1, fetchcounter_1_step2, fetchcounter_1_step3;

  FetchCounter fetchcounter_1 (
    .CLK(CLK), .Reset(Reset), .Step1(fetchcounter_1_step1), .Step2(fetchcounter_1_step2),
    .Step3(fetchcounter_1_step3));  // open: Step4, Step5, Step6
  and and_1 (MARwrite, fetchcounter_1_step1, FetchEnable);
  and and_2 (MBRwrite, fetchcounter_1_step2, FetchEnable);
  and and_3 (IRwrite, fetchcounter_1_step3, FetchEnable);

  assign PCinc = MARwrite;
  assign PCread = MARwrite;
  assign RAMread = MBRwrite;
endmodule

module FetchCounter (
  input  CLK,
  input  Reset,
  output Step1,
  output Step2,
  output Step3,
  output Step4,
  output Step5,
  output Step6
);

  wire and_1_out, or_1_out, or_2_out, or_3_out, or_4_out, or_5_out, or_6_out;

  or or_1 (or_1_out, Step6, Step1);
  and and_1 (and_1_out, CLK, ~1'b0);  // AND_Gate
  or or_2 (or_2_out, Step1, Step2);
  T_Flip_Flop #(.trigger("falling")) t_ff_1 (
    .T(or_1_out), .clk(and_1_out), .Q(Step1), .preset(Reset));  // open: Qn, reset
  or or_3 (or_3_out, Step2, Step3);
  T_Flip_Flop #(.trigger("falling")) t_ff_2 (
    .T(or_2_out), .clk(and_1_out), .Q(Step2), .reset(Reset));  // open: Qn, preset
  or or_4 (or_4_out, Step3, Step4);
  T_Flip_Flop #(.trigger("falling")) t_ff_3 (
    .T(or_3_out), .clk(and_1_out), .Q(Step3), .reset(Reset));  // open: Qn, preset
  or or_5 (or_5_out, Step4, Step5);
  T_Flip_Flop #(.trigger("falling")) t_ff_4 (
    .T(or_4_out), .clk(and_1_out), .Q(Step4), .reset(Reset));  // open: Qn, preset
  T_Flip_Flop #(.trigger("falling")) t_ff_5 (
    .T(or_5_out), .clk(and_1_out), .Q(Step5), .reset(Reset));  // open: Qn, preset
  or or_6 (or_6_out, Step5, Step6);
  T_Flip_Flop #(.trigger("falling")) t_ff_6 (
    .T(or_6_out), .clk(and_1_out), .Q(Step6), .reset(Reset));  // open: Qn, preset
endmodule

module Left (
  input  Len,
  input  Clk,
  input  Lread,
  input  D1in,
  input  D2in,
  input  D3in,
  input  D4in,
  output D1out,
  output D2out,
  output D3out,
  output D4out
);

  wire and_1_out, d_ff_1_q, d_ff_2_q, d_ff_3_q, d_ff_4_q, undriven;

  and and_1 (and_1_out, Len, Clk);
  D_Flip_Flop #(.trigger("falling")) d_ff_1 (.D(D1in), .clk(and_1_out), .Q(d_ff_1_q));  // open: Qn, preset, reset
  D_Flip_Flop #(.trigger("falling")) d_ff_2 (
    .D(D2in), .clk(and_1_out), .Q(d_ff_2_q), .reset(undriven));  // open: Qn, preset
  D_Flip_Flop #(.trigger("falling")) d_ff_3 (.D(D3in), .clk(and_1_out), .Q(d_ff_3_q));  // open: Qn, preset, reset
  D_Flip_Flop #(.trigger("falling")) d_ff_4 (.D(D4in), .clk(and_1_out), .Q(d_ff_4_q));  // open: Qn, preset, reset
  and and_2 (D1out, Lread, d_ff_1_q);
  and and_3 (D2out, Lread, d_ff_2_q);
  and and_4 (D3out, Lread, d_ff_3_q);
  and and_5 (D4out, Lread, d_ff_4_q);
endmodule

module Right (
  input  Ren,
  input  Clk,
  input  Rread,
  input  D1in,
  input  D2in,
  input  D3in,
  input  D4in,
  output D1out,
  output D2out,
  output D3out,
  output D4out
);

  wire and_1_out, d_ff_1_q, d_ff_2_q, d_ff_3_q, d_ff_4_q, undriven;

  and and_1 (and_1_out, Ren, Clk);
  D_Flip_Flop #(.trigger("falling")) d_ff_1 (.D(D1in), .clk(and_1_out), .Q(d_ff_1_q));  // open: Qn, preset, reset
  D_Flip_Flop #(.trigger("falling")) d_ff_2 (
    .D(D2in), .clk(and_1_out), .Q(d_ff_2_q), .reset(undriven));  // open: Qn, preset
  D_Flip_Flop #(.trigger("falling")) d_ff_3 (.D(D3in), .clk(and_1_out), .Q(d_ff_3_q));  // open: Qn, preset, reset
  D_Flip_Flop #(.trigger("falling")) d_ff_4 (.D(D4in), .clk(and_1_out), .Q(d_ff_4_q));  // open: Qn, preset, reset
  and and_2 (D1out, Rread, d_ff_1_q);
  and and_3 (D2out, Rread, d_ff_2_q);
  and and_4 (D3out, Rread, d_ff_3_q);
  and and_5 (D4out, Rread, d_ff_4_q);
endmodule
